// Logisim project Ficha 6 exercicio 1.circ as structural Verilog: 1 circuit, main circuit main
module main (
  input  A,
  input  B,
  input  A_2,
  input  B_2,
  input  A_3,
  input  B_3,
  input  A_4,
  input  B_4,
  input  Ci,
  output Co,
  output S,
  output S_2,
  output S_3,
  output S_4
);

  wire and_1_out, and_2_out, and_3_out, and_4_out, and_5_out, and_6_out, and_7_out, and_8_out, or_1_out,
       or_2_out, or_3_out, xor_2_out, xor_5_out, xor_7_out;

  and and_1 (and_1_out, A_4, B_4);
  xor xor_1 (Ci, B_4, A_4);
  and and_2 (and_2_out, Ci, Ci);
  and and_3 (and_3_out, A_3, B_3);
  xor xor_2 (xor_2_out, B_3, A_3);
  or or_1 (or_1_out, and_1_out, and_2_out);
  xor xor_3 (S_4, Ci, Ci);
  and and_4 (and_4_out, xor_2_out, or_1_out);
  or or_2 (or_2_out, and_3_out, and_4_out);
  xor xor_4 (S_3, xor_2_out, or_1_out);
  and and_5 (and_5_out, A_2, B_2);
  xor xor_5 (xor_5_out, B_2, A_2);
  and and_6 (and_6_out, xor_5_out, or_2_out);
  and and_7 (and_7_out, A, B);
  or or_3 (or_3_out, and_5_out, and_6_out);
  xor xor_6 (S_2, xor_5_out, or_2_out);
  xor xor_7 (xor_7_out, B, A);
  and and_8 (and_8_out, xor_7_out, or_3_out);
  or or_4 (Co, and_7_out, and_8_out);
  xor xor_8 (S, xor_7_out, or_3_out);
endmodule
