// Logisim project Máquina de café.circ as structural Verilog: 1 circuit, main circuit main
module main (
  input  M1,
  input  M2,
  input  B,
  output out_4,
  output out_5,
  output out_6,
  output T0,
  output T2,
  output T3,
  output T1
);

  wire and_1_out, and_2_out, and_3_out, and_4_out, and_5_out, and_6_out, and_7_out, and_8_out, and_9_out,
       and_10_out, and_11_out, and_12_out, and_13_out, and_14_out, and_15_out, and_16_out, and_17_out,
       and_18_out, and_19_out, and_20_out, and_21_out, and_22_out, and_23_out, and_24_out, and_25_out,
       and_26_out, and_27_out, and_28_out, and_29_out, and_30_out, and_31_out, and_32_out, and_33_out,
       and_34_out, and_35_out, and_36_out, and_37_out, and_38_out, and_39_out, and_40_out, and_41_out,
       and_42_out, b_out, c_out, clock_1_out, d_ff_1_q, d_ff_1_qn, d_ff_2_q, d_ff_2_qn, d_ff_3_q, d_ff_4_q,
       d_ff_4_qn, d_ff_5_q, d_ff_5_qn, d_ff_6_qn, d_out, e_out, f_out, g_out, not_1_out, not_2_out,
       not_3_out, not_4_out, not_5_out, not_6_out, or_1_out, or_3_out, or_5_out, or_7_out, or_9_out,
       or_11_out, xor_1_out;

  Clock clock_1 (.out(clock_1_out));
  not not_1 (not_1_out, M2);
  not not_2 (not_2_out, M1);
  not not_3 (not_3_out, out_4);
  not not_4 (not_4_out, out_5);
  and and_1 (and_1_out, M1, d_ff_1_qn);
  and and_2 (and_2_out, not_1_out, not_2_out, d_ff_1_q, d_ff_2_qn);
  and and_3 (and_3_out, M2, d_ff_2_q, d_ff_1_qn);
  and and_4 (and_4_out, M2, d_ff_2_qn, d_ff_1_q);
  and and_5 (and_5_out, d_ff_2_qn, d_ff_1_q);
  not not_5 (not_5_out, out_6);
  or or_1 (or_1_out, and_1_out, and_2_out, and_3_out, and_4_out);
  or or_2 (out_4, d_ff_3_q, and_5_out);
  D_Flip_Flop d_ff_1 (.clk(clock_1_out), .D(or_1_out), .Q(d_ff_1_q), .Qn(d_ff_1_qn));  // open: preset, en, reset
  and and_6 (and_6_out, not_5_out, not_4_out, not_3_out);
  and and_7 (and_7_out, not_3_out, out_5, not_5_out);
  and and_8 (and_8_out, not_3_out, not_4_out, out_6);
  and and_9 (and_9_out, not_3_out, not_4_out, not_5_out);
  and and_10 (and_10_out, out_4, not_4_out, not_5_out);
  and and_11 (and_11_out, not_3_out, out_5, not_5_out);
  and and_12 (and_12_out, not_3_out, not_4_out, out_6);
  and and_13 (and_13_out, d_ff_2_q, d_ff_1_qn);
  or or_3 (or_3_out, and_6_out, and_7_out, and_8_out);
  or u_b (b_out, and_9_out, and_10_out, and_11_out, and_12_out);
  or or_4 (out_5, d_ff_3_q, and_13_out);
  and and_14 (and_14_out, out_6, not_3_out, not_4_out);
  and and_15 (and_15_out, out_4, not_4_out, not_5_out);
  and and_16 (and_16_out, not_3_out, not_4_out, not_5_out);
  and and_17 (and_17_out, d_ff_2_q, d_ff_1_qn);
  and and_18 (and_18_out, M2, d_ff_2_qn);
  and and_19 (and_19_out, d_ff_1_q, not_1_out, M1, d_ff_2_qn);
  and and_20 (and_20_out, d_ff_2_q, d_ff_1_q);
  or c (c_out, and_14_out, and_15_out, and_16_out);
  or or_5 (or_5_out, and_17_out, and_18_out, and_19_out);
  or or_6 (out_6, d_ff_3_q, and_20_out);
  D_Flip_Flop d_ff_2 (.clk(clock_1_out), .D(or_5_out), .Q(d_ff_2_q), .Qn(d_ff_2_qn));  // open: preset, en, reset
  and and_21 (and_21_out, not_3_out, not_4_out, out_6);
  and and_22 (and_22_out, not_3_out, out_5, not_5_out);
  and and_23 (and_23_out, not_3_out, not_4_out, not_5_out);
  and and_24 (and_24_out, d_ff_2_q, d_ff_1_q);
  or or_7 (or_7_out, and_24_out, d_ff_3_q);
  _7_Segment_Display u_7_segment_display_1 (
    .g(g_out), .f(f_out), .a(or_3_out), .b(b_out), .e(e_out), .d(d_out), .c(c_out));  // open: dp
  or d (d_out, and_21_out, and_22_out, and_23_out);
  D_Flip_Flop d_ff_3 (.clk(clock_1_out), .D(or_7_out), .Q(d_ff_3_q));  // open: Qn, preset, en, reset
  LED led_1 (.in(d_ff_3_q));
  not not_6 (not_6_out, d_ff_3_q);
  and and_25 (and_25_out, out_5, not_3_out, not_5_out);
  and and_26 (and_26_out, not_4_out, not_3_out, not_5_out);
  or e (e_out, and_25_out, and_26_out);
  and and_27 (and_27_out, d_ff_3_q, T3);
  and and_28 (and_28_out, d_ff_3_q, B, d_ff_4_qn);
  and and_29 (and_29_out, not_6_out, d_ff_5_q, d_ff_4_qn);
  and and_30 (and_30_out, not_6_out, B, d_ff_6_qn, d_ff_4_qn);
  and and_31 (and_31_out, d_ff_5_qn, d_ff_4_q);
  or or_8 (T0, and_31_out, and_32_out);
  and and_32 (and_32_out, T3, d_ff_5_q);
  and f (f_out, not_3_out, not_4_out, not_5_out);
  or or_9 (or_9_out, and_27_out, and_28_out, and_29_out, and_30_out);
  D_Flip_Flop d_ff_4 (.clk(clock_1_out), .D(or_9_out), .Q(d_ff_4_q), .Qn(d_ff_4_qn));  // open: preset, en, reset
  and and_33 (and_33_out, T3, d_ff_4_q);
  and and_34 (and_34_out, d_ff_4_qn, d_ff_5_q);
  and and_35 (and_35_out, not_3_out, not_4_out, out_6);
  and and_36 (and_36_out, not_3_out, out_5, not_5_out);
  D_Flip_Flop d_ff_5 (.clk(clock_1_out), .D(xor_1_out), .Q(d_ff_5_q), .Qn(d_ff_5_qn));  // open: preset, en, reset
  xor xor_1 (xor_1_out, d_ff_4_q, d_ff_5_q);
  or or_10 (T1, and_33_out, and_34_out);
  or g (g_out, and_35_out, and_36_out);
  and and_37 (and_37_out, d_ff_4_q, d_ff_5_q);
  and and_38 (and_38_out, not_6_out, T3, d_ff_5_q);
  and and_39 (and_39_out, d_ff_3_q, T3);
  and and_40 (and_40_out, d_ff_5_q, d_ff_4_q);
  and and_41 (and_41_out, d_ff_4_q, T3);
  and and_42 (and_42_out, d_ff_5_q, T3);
  or or_11 (or_11_out, and_37_out, and_38_out, and_39_out);
  D_Flip_Flop d_ff_6 (.clk(clock_1_out), .D(or_11_out), .Q(T3), .Qn(d_ff_6_qn));  // open: preset, en, reset
  or or_12 (T2, and_40_out, and_41_out, and_42_out);
  LED led_2 (.in(T3));

  // Notes on the sheet:
  //   Clock
  //   S0
  //   S1
  //   S2
  //   D0
  //   S0
  //   Moedeiro
  //   S1
  //   a
  //   S2
  //   D1
  //   D2
  //   l
  //   Módulo para café
  //   D0
  //   D1
  //   D2
endmodule
